// Logisim project sr_latch.circ as structural Verilog: 6 circuits, main circuit main
module main (
  output Q,
  output Q2
);

  wire R_out, S_out;

  Button S (.out(S_out));
  Button R (.out(R_out));
  nor nor_1 (Q, S_out, Q2);
  nor nor_2 (Q2, Q, R_out);

  // Notes on the sheet:
  //   SR Latch
endmodule

module d_latch (
  input  Set,
  input  Enable,
  output Q
);

  wire and_1_out, and_2_out, nor_2_out, not_1_out;

  not not_1 (not_1_out, Set);
  and and_1 (and_1_out, not_1_out, Enable);
  and and_2 (and_2_out, Enable, Set);
  nor nor_1 (Q, and_1_out, nor_2_out);
  nor nor_2 (nor_2_out, Q, and_2_out);

  // Notes on the sheet:
  //   D Latch
endmodule

module REG_8BIT (
  input  [7:0] inp,
  input  load,
  output [7:0] out_3
);

  d_latch d_latch_1 (.Set(inp[0]), .Enable(load), .Q(out_3[0]));
  d_latch d_latch_2 (.Set(inp[1]), .Enable(load), .Q(out_3[1]));
  d_latch d_latch_3 (.Set(inp[2]), .Enable(load), .Q(out_3[2]));
  d_latch d_latch_4 (.Set(inp[3]), .Enable(load), .Q(out_3[3]));
  d_latch d_latch_5 (.Set(inp[4]), .Enable(load), .Q(out_3[4]));
  d_latch d_latch_6 (.Set(inp[5]), .Enable(load), .Q(out_3[5]));
  d_latch d_latch_7 (.Set(inp[6]), .Enable(load), .Q(out_3[6]));
  d_latch d_latch_8 (.Set(inp[7]), .Enable(load), .Q(out_3[7]));
endmodule

module RAM_8BYTE (
  input  [7:0] iinp,
  input  [2:0] address,
  input  load,
  output [7:0] data
);

  wire demultiplexer_1_out0, demultiplexer_1_out1, demultiplexer_1_out2, demultiplexer_1_out3,
       demultiplexer_1_out4, demultiplexer_1_out5, demultiplexer_1_out6, demultiplexer_1_out7;
  wire [7:0] reg_8bit_1_out_3, reg_8bit_2_out_3, reg_8bit_3_out_3, reg_8bit_4_out_3, reg_8bit_5_out_3,
       reg_8bit_6_out_3, reg_8bit_7_out_3, reg_8bit_8_out_3;

  Demultiplexer #(.select(3)) demultiplexer_1 (
    .out0(demultiplexer_1_out0), .out1(demultiplexer_1_out1), .out2(demultiplexer_1_out2),
    .out3(demultiplexer_1_out3), .out4(demultiplexer_1_out4), .out5(demultiplexer_1_out5),
    .out6(demultiplexer_1_out6), .out7(demultiplexer_1_out7), .in(load), .sel(address));
  LED led_1 (.in(demultiplexer_1_out0));
  LED led_2 (.in(demultiplexer_1_out1));
  LED led_3 (.in(demultiplexer_1_out2));
  LED led_4 (.in(demultiplexer_1_out3));
  LED led_5 (.in(demultiplexer_1_out4));
  LED led_6 (.in(demultiplexer_1_out5));
  LED led_7 (.in(demultiplexer_1_out6));
  LED led_8 (.in(demultiplexer_1_out7));
  REG_8BIT reg_8bit_1 (.inp(iinp), .load(demultiplexer_1_out0), .out_3(reg_8bit_1_out_3));
  REG_8BIT reg_8bit_2 (.inp(iinp), .load(demultiplexer_1_out1), .out_3(reg_8bit_2_out_3));
  REG_8BIT reg_8bit_3 (.inp(iinp), .load(demultiplexer_1_out2), .out_3(reg_8bit_3_out_3));
  REG_8BIT reg_8bit_4 (.inp(iinp), .load(demultiplexer_1_out3), .out_3(reg_8bit_4_out_3));
  REG_8BIT reg_8bit_5 (.inp(iinp), .load(demultiplexer_1_out4), .out_3(reg_8bit_5_out_3));
  REG_8BIT reg_8bit_6 (.inp(iinp), .load(demultiplexer_1_out5), .out_3(reg_8bit_6_out_3));
  REG_8BIT reg_8bit_7 (.inp(iinp), .load(demultiplexer_1_out6), .out_3(reg_8bit_7_out_3));
  REG_8BIT reg_8bit_8 (.inp(iinp), .load(demultiplexer_1_out7), .out_3(reg_8bit_8_out_3));
  Multiplexer #(.select(3), .width(8)) multiplexer_1 (
    .in0(reg_8bit_1_out_3), .in1(reg_8bit_2_out_3), .in2(reg_8bit_3_out_3), .in3(reg_8bit_4_out_3),
    .in4(reg_8bit_5_out_3), .in5(reg_8bit_6_out_3), .in6(reg_8bit_7_out_3), .in7(reg_8bit_8_out_3),
    .out(data), .sel(address));
endmodule

module RAM_64BYTE (
  input  [7:0] inp,
  input  [5:0] address,
  input  load,
  output [7:0] data
);

  wire demultiplexer_1_out0, demultiplexer_1_out1, demultiplexer_1_out2, demultiplexer_1_out3,
       demultiplexer_1_out4, demultiplexer_1_out5, demultiplexer_1_out6, demultiplexer_1_out7;
  wire [7:0] ram_8byte_1_data, ram_8byte_2_data, ram_8byte_3_data, ram_8byte_4_data, ram_8byte_5_data,
       ram_8byte_6_data, ram_8byte_7_data, ram_8byte_8_data;

  Demultiplexer #(.select(3)) demultiplexer_1 (
    .out0(demultiplexer_1_out0), .out1(demultiplexer_1_out1), .out2(demultiplexer_1_out2),
    .out3(demultiplexer_1_out3), .out4(demultiplexer_1_out4), .out5(demultiplexer_1_out5),
    .out6(demultiplexer_1_out6), .out7(demultiplexer_1_out7), .in(load), .sel(address[5:3]));
  RAM_8BYTE ram_8byte_1 (.iinp(inp), .address(address[2:0]), .load(demultiplexer_1_out0), .data(ram_8byte_1_data));
  RAM_8BYTE ram_8byte_2 (.iinp(inp), .address(address[2:0]), .load(demultiplexer_1_out1), .data(ram_8byte_2_data));
  RAM_8BYTE ram_8byte_3 (.iinp(inp), .address(address[2:0]), .load(demultiplexer_1_out2), .data(ram_8byte_3_data));
  RAM_8BYTE ram_8byte_4 (.iinp(inp), .address(address[2:0]), .load(demultiplexer_1_out3), .data(ram_8byte_4_data));
  RAM_8BYTE ram_8byte_5 (.iinp(inp), .address(address[2:0]), .load(demultiplexer_1_out4), .data(ram_8byte_5_data));
  RAM_8BYTE ram_8byte_6 (.iinp(inp), .address(address[2:0]), .load(demultiplexer_1_out5), .data(ram_8byte_6_data));
  RAM_8BYTE ram_8byte_7 (.iinp(inp), .address(address[2:0]), .load(demultiplexer_1_out6), .data(ram_8byte_7_data));
  RAM_8BYTE ram_8byte_8 (.iinp(inp), .address(address[2:0]), .load(demultiplexer_1_out7), .data(ram_8byte_8_data));
  Multiplexer #(.select(3), .width(8)) multiplexer_1 (
    .in0(ram_8byte_1_data), .in1(ram_8byte_2_data), .in2(ram_8byte_3_data), .in3(ram_8byte_4_data),
    .in4(ram_8byte_5_data), .in5(ram_8byte_6_data), .in6(ram_8byte_7_data), .in7(ram_8byte_8_data),
    .out(data), .sel(address[5:3]));
endmodule

module ProgramCounter (
  input  reset,
  input  [7:0] inp,
  input  inc,
  output [7:0] out_4
);

  wire clock_1_out;
  wire [7:0] adder_1_out, multiplexer_1_out, multiplexer_2_out;

  Adder adder_1 (.a(out_4), .b(8'h1), .out(adder_1_out));  // open: cin, cout
  Multiplexer #(.width(8)) multiplexer_1 (.in0(inp), .in1(adder_1_out), .out(multiplexer_1_out), .sel(inc));
  Multiplexer #(.width(8)) multiplexer_2 (
    .in0(multiplexer_1_out), .in1({8{1'b0}}), .out(multiplexer_2_out), .sel(reset));
  Clock clock_1 (.out(clock_1_out));
  REG_8BIT reg_8bit_1 (.inp(multiplexer_2_out), .load(clock_1_out), .out_3(out_4));
endmodule
